# Fritzing sketch syringepump_sketch (saved by Fritzing 0.9.3b)

parts:
  DC_Mot_Enc1 = DC Motor with two-phase hall-encoder [part_number=VT-E-G25A-06-177E]
  S1 = H-Bridge with L298N
  Part1 = Arduino Uno (Rev3) - ICSP
  VCC1 = Battery
  VCC2 = Battery
  J1 = Infrared Proximity Sensor

nets:
  N1: DC_Mot_Enc1.pin1, S1.M1-01
  N2: DC_Mot_Enc1.pin2, S1.M1-02, Part1.A5/SCL, J1.Vout
  GND: DC_Mot_Enc1.pin3, S1.GND, Part1.GND, VCC1.-, VCC2.-, J1.GND
  N3: DC_Mot_Enc1.pin4, Part1.3V3
  N4: DC_Mot_Enc1.pin5, Part1.D2
  N5: DC_Mot_Enc1.pin6, Part1.D3_PWM
  N6: S1.12V, VCC1.+, VCC2.+
  N7: S1.ENA, Part1.D10_PWM/SS
  N8: S1.IN1, Part1.D6_PWM
  N9: S1.IN2, Part1.D7
  N10: Part1.ICSP_MISO, Part1.D12/MISO
  5V: Part1.5V, J1.Vcc

custom parts:
  H-Bridge with L298N: h-bridge
